# Fritzing sketch Arduino Gas Module (saved by Fritzing 0.9.4)
breadboards: 1

parts:
  Part1 = Arduino Nano (Rev3.0)
  MQ2 = GAS_SENSOR [package=mq-3]
  LED1 = smd LED [color="Red (633nm)" package="1206 [SMD]"]
  LED2 = smd LED [color="Green (565nm)" package="1206 [SMD]"]
  S1 = Pushbutton [package="[THT]"]
  S2 = Pushbutton [package="[THT]"]
  S3 = Pushbutton [package="[THT]"]
  U1 = LCD-16X2 [package=lcd-16x2]
  LCM1602_IIC1 = LCM1602 IIC [part_number="LCM1602 IIC" chip_label="LCM1602 IIC" package="DIP (Dual Inline) [THT]"]
  J1 = Piezo Speaker

nets:
  GND: Part1.GND, LED1.cathode, LED2.cathode, S1.Pin_1, S1.Pin_2, S2.Pin_1, S2.Pin_2, S3.Pin_1, S3.Pin_2, LCM1602_IIC1.GND, J1.pin1
  N1: Part1.D2, LED1.anode
  N2: Part1.D3, LED2.anode
  N3: Part1.D5, S1.Pin_3, S1.Pin_4
  N4: Part1.D6, S2.Pin_3, S2.Pin_4
  N5: Part1.D7, S3.Pin_3, S3.Pin_4
  N6: Part1.D12/MISO, J1.pin2
  5V: Part1.5V, MQ2.B1, LCM1602_IIC1.VCC
  N7: Part1.A5, LCM1602_IIC1.SCL
  N8: Part1.A4, LCM1602_IIC1.SDA
  N9: Part1.A0, MQ2.A1
  VSS: U1.VSS, LCM1602_IIC1.VSS
  VDD: U1.VDD, LCM1602_IIC1.VDD
  N10: U1.VO, LCM1602_IIC1.V0
  N11: U1.RS, LCM1602_IIC1.RS
  N12: U1.R_W, LCM1602_IIC1.RW
  N13: U1.E, LCM1602_IIC1.E
  N14: U1.DB0, LCM1602_IIC1.D0
  N15: U1.DB1, LCM1602_IIC1.D1
  N16: U1.DB2, LCM1602_IIC1.D2
  N17: U1.DB3, LCM1602_IIC1.D3
  N18: U1.DB4, LCM1602_IIC1.D4
  N19: U1.DB5, LCM1602_IIC1.D5
  N20: U1.DB6, LCM1602_IIC1.D6
  N21: U1.DB7, LCM1602_IIC1.D7
  N22: U1.A, LCM1602_IIC1.A
  N23: U1.K, LCM1602_IIC1.K

custom parts:
  LCM1602 IIC: I2C-Module to use a 1602 or 2004 LCD on with the wire.h libory Serial LCD Modul
